# Fritzing sketch New Circuit (saved by Fritzing 0.9.6b)

parts:
  SmartDriveDuo10A1 = MDDS10
  Part1 = Arduino Uno (Rev3)
  S1 = Round Pushbutton
  M1 = DC Motor  # not connected
  M2 = DC Motor  # not connected
  S2 = SWITCH-MOMENTARY-2 [package=tactile-switch-1101ne]
  VCC1 = Battery block 9V
  R1 = Resistor [tolerance=±5% power=0.25 resistance=220 package=THT]

nets:
  N1: SmartDriveDuo10A1.no_name_yet#connector_AN1, Part1.D5_PWM
  N2: SmartDriveDuo10A1.no_name_yet#connector_AN2, Part1.D6_PWM
  N3: SmartDriveDuo10A1.no_name_yet#connector_B1, S2.1
  N4: SmartDriveDuo10A1.no_name_yet#connector_DIG1, Part1.D2
  N5: SmartDriveDuo10A1.no_name_yet#connector_DIG2, Part1.D3_PWM
  N6: SmartDriveDuo10A1.no_name_yet#connector_GND0, Part1.GND, R1.Pin_0
  N7: SmartDriveDuo10A1.no_name_yet#connector_V5, Part1.5V, S1.leg1
  N8: Part1.D7, R1.Pin_1
  N9: S2.2, VCC1.+
